// Logisim project alu.circ as structural Verilog: 1 circuit, main circuit main
module main (
  input  D_IN,
  input  ACC,
  input  OP_0,
  input  OP_1,
  input  OP_2,
  input  OP_3,
  input  ADD,
  input  C_IN,
  input  ONE,
  input  TWO,
  output ACC_OUT,
  output CARRY_OUT
);

  wire and_1_out, and_2_out, nand_1_out, nand_2_out, nand_3_out, nand_4_out, nand_5_out, nand_6_out,
       nand_7_out, nor_1_out, not_1_out, not_2_out, not_3_out, or_1_out, xor_1_out, xor_2_out;

  not not_1 (not_1_out, D_IN);
  not not_2 (not_2_out, ACC);
  xor xor_1 (xor_1_out, ACC, D_IN);
  and and_1 (and_1_out, xor_1_out, C_IN);
  and and_2 (and_2_out, ACC, D_IN);
  nand nand_1 (nand_1_out, not_2_out, not_1_out, OP_0);
  nand nand_2 (nand_2_out, ACC, not_1_out, OP_1);
  nand nand_3 (nand_3_out, not_2_out, D_IN, OP_2);
  nand nand_4 (nand_4_out, ACC, D_IN, OP_3);
  xor xor_2 (xor_2_out, xor_1_out, C_IN);
  or or_1 (or_1_out, and_1_out, and_2_out);
  nor nor_1 (nor_1_out, ADD, ONE);
  not not_3 (not_3_out, TWO);
  nand nand_5 (nand_5_out, ADD, xor_2_out);
  nand nand_6 (nand_6_out, or_1_out, ADD);
  nand nand_7 (nand_7_out, C_IN, nor_1_out);
  nand nand_8 (ACC_OUT, nand_1_out, nand_2_out, nand_3_out, nand_4_out, nand_5_out);
  nand nand_9 (CARRY_OUT, nand_6_out, nand_7_out, not_3_out);
endmodule
